// Logisim project Z80.circ as structural Verilog
module CPU_ALU (
  input  [7:0] b,
  input  [7:0] a,
  input  carry_in,
  input  [4:0] op_code,
  output FLAG_P_V,
  output FLAG_C,
  output FLAG_N,
  output FLAG_Z,
  output [7:0] C,
  output FLAG_H,
  output FLAG_S
);

  wire and_1_out, CPU_ALU_OPCODE_DECODER_5_1_o_gr_0, CPU_ALU_OPCODE_DECODER_5_1_o_gr_1, not_1_out;
  wire [2:0] CPU_ALU_OPCODE_DECODER_5_1_o_code;

  CPU_ALU_OPCODE_DECODER_5 CPU_ALU_OPCODE_DECODER_5_1 (
    .op_code(op_code), .o_code(CPU_ALU_OPCODE_DECODER_5_1_o_code),
    .o_gr_0(CPU_ALU_OPCODE_DECODER_5_1_o_gr_0), .o_gr_1(CPU_ALU_OPCODE_DECODER_5_1_o_gr_1));
  not not_1 (not_1_out, CPU_ALU_OPCODE_DECODER_5_1_o_gr_0);
  and and_1 (and_1_out, not_1_out, CPU_ALU_OPCODE_DECODER_5_1_o_gr_1);
  // CPU_ALU_OP_GR_10 CPU_ALU_OP_GR_10_1: pin names not known; wires that end beside it: a, b, carry_in, CPU_ALU_OPCODE_DECODER_5_1_o_code, and_1_out, FLAG_P_V, FLAG_C, FLAG_N, FLAG_Z, C, FLAG_H, FLAG_S

  // Notes on the sheet:
  //   FLAG_P_V: pull=down
  //   FLAG_C: pull=down
  //   FLAG_N: pull=down
  //   FLAG_Z: pull=down
  //   FLAG_H: pull=down
  //   FLAG_S: pull=down
  //   C: pull=down
  //   carry_in: pull=down
  //   ACCUMULATOR INPUT
  //   GROUP[2]OPERATION[3]
  //   OPERAND REGISTER
  //   Core ALU
  //   Group 10x
  //   TBD Non-Core ALU - Group 00x
  //   TBD Non-Core ALU - Group 10x
  //   (Parity/Overflow)
  //   (Carry)
  //   (ADD=0, SUB=1)
  //   (Zero)
  //   (Half-Carry)
  //   (Sign)
endmodule

module CPU_ALU_OP_GR_10 (
  input  [7:0] A,
  input  [7:0] B,
  input  carry_in,
  input  [2:0] op_code,
  input  group_enable,
  output FLAG_P_V,
  output FLAG_C,
  output FLAG_N,
  output FLAG_Z,
  output FLAG_H,
  output FLAG_S,
  output [7:0] C
);

  wire and_1_out, and_2_out, and_3_out, and_4_out, and_5_out, and_6_out;
  wire [7:0] cpu_decoder_3x8_1_o;

  CPU_DECODER_3x8 cpu_decoder_3x8_1 (.i(op_code), .o(cpu_decoder_3x8_1_o));
  and and_1 (and_1_out, cpu_decoder_3x8_1_o[0], group_enable);
  CPU_AND cpu_and_1 (
    .a(A), .b(B), .Enable(and_2_out), .C(C), .FLAG_Z(FLAG_Z), .FLAG_H(FLAG_H), .FLAG_C(FLAG_C),
    .FLAG_N(FLAG_N), .FLAG_P_V(FLAG_P_V), .FLAG_S(FLAG_S));
  CPU_ADD cpu_add_1 (
    .A(A), .B(B), .carry_in(carry_in), .Enable(and_1_out), .FLAG_P_V(FLAG_P_V), .FLAG_C(FLAG_C),
    .FLAG_N(FLAG_N), .FLAG_Z(FLAG_Z), .C(C), .FLAG_H(FLAG_H), .FLAG_S(FLAG_S));
  and and_2 (and_2_out, cpu_decoder_3x8_1_o[1], group_enable);
  and and_3 (and_3_out, cpu_decoder_3x8_1_o[2], group_enable);
  CPU_OR cpu_or_1 (
    .a(A), .b(B), .Enable(and_4_out), .C(C), .FLAG_Z(FLAG_Z), .FLAG_H(FLAG_H), .FLAG_P_V(FLAG_P_V),
    .FLAG_S(FLAG_S), .FLAG_N(FLAG_N), .FLAG_C(FLAG_C));
  CPU_SUB cpu_sub_1 (
    .A(A), .B(B), .Enable(and_3_out), .FLAG_P_V(FLAG_P_V), .FLAG_C(FLAG_C), .FLAG_N(FLAG_N), .FLAG_Z(FLAG_Z),
    .C(C), .FLAG_H(FLAG_H), .FLAG_S(FLAG_S));
  and and_4 (and_4_out, cpu_decoder_3x8_1_o[3], group_enable);
  CPU_XOR cpu_xor_1 (
    .a(A), .b(B), .Enable(and_6_out), .FLAG_S(FLAG_S), .c(C), .FLAG_Z(FLAG_Z), .FLAG_P_V(FLAG_P_V),
    .FLAG_C(FLAG_C), .FLAG_N(FLAG_N), .FLAG_H(FLAG_H));
  CPU_CP cpu_cp_1 (
    .A(A), .B(B), .Enable(and_5_out), .C(C), .FLAG_P_V(FLAG_P_V), .FLAG_C(FLAG_C), .FLAG_N(FLAG_N),
    .FLAG_Z(FLAG_Z), .FLAG_H(FLAG_H), .FLAG_S(FLAG_S));
  and and_5 (and_5_out, cpu_decoder_3x8_1_o[7], group_enable);
  and and_6 (and_6_out, cpu_decoder_3x8_1_o[5], group_enable);

  // Other names for the same wires on the sheet: c_out[7:0] = C; f_c = FLAG_C; f_h = FLAG_H; f_n = FLAG_N;
  //   f_pv = FLAG_P_V; f_s = FLAG_S; f_z = FLAG_Z

  // Notes on the sheet:
  //   B: pull=down
  //   op_code: pull=down
  //   group_enable: pull=down
  //   A: pull=down
  //   carry_in: pull=down
  //   FLAG_N: pull=down
  //   FLAG_Z: pull=down
  //   FLAG_H: pull=down
  //   FLAG_S: pull=down
  //   FLAG_P_V: pull=down
  //   FLAG_C: pull=down
  //   C: pull=down
  //   ADD - 000
  //   (Carry)
  //   (Zero)
  //   (Half-Carry)
  //   (Sign)
  //   AND - 100
  //   (Parity/Overflow)
  //   (ADD=0, SUB=1)
  //   SUB - 010
  //   OR - 110
  //   CP - 111
  //   XOR - 101
endmodule

module CPU_ALU_OPCODE_DECODER_5 (
  input  [4:0] op_code,
  output [2:0] o_code,
  output o_gr_0,
  output o_gr_1
);


  assign o_code = op_code[2:0];
  assign o_gr_0 = op_code[3];
  assign o_gr_1 = op_code[4];

  // Notes on the sheet:
  //   o_code: pull=down
endmodule

module CPU_ALU_OVERFLOW (
  input  [7:0] a,
  input  [7:0] b,
  input  [7:0] inp,
  output overflw
);

  wire and_1_out, and_2_out, not_1_out, not_2_out, not_3_out;

  not not_1 (not_1_out, a[7]);
  not not_2 (not_2_out, b[7]);
  not not_3 (not_3_out, inp[7]);
  and and_1 (and_1_out, not_1_out, not_2_out, inp[7]);
  and and_2 (and_2_out, b[7], a[7], not_3_out);
  or or_1 (overflw, and_1_out, and_2_out);
endmodule

module CPU_ALU_SIGN_8 (
  input  [7:0] i,
  output negative
);


  assign negative = i[7];
endmodule

module CPU_ADD (
  input  [7:0] A,
  input  [7:0] B,
  input  carry_in,
  input  Enable,
  output FLAG_P_V,
  output FLAG_C,
  output FLAG_N,
  output FLAG_Z,
  output [7:0] C,
  output FLAG_H,
  output FLAG_S
);

  wire CPU_ADDER_8_1_carry_out, CPU_ADDER_8_1_half_carry_out, CPU_ALU_OVERFLOW_1_overflw,
       CPU_ALU_SIGN_8_1_negative, CPU_Z_1_o;
  wire [7:0] CPU_ADDER_8_1_output_bus_1;

  CPU_ADDER_8 CPU_ADDER_8_1 (
    .a(A), .b(B), .carry_in(carry_in), .carry_out(CPU_ADDER_8_1_carry_out),
    .half_carry_out(CPU_ADDER_8_1_half_carry_out), .Output_bus_1(CPU_ADDER_8_1_output_bus_1));
  CPU_ALU_OVERFLOW CPU_ALU_OVERFLOW_1 (
    .a(A), .b(B), .inp(CPU_ADDER_8_1_output_bus_1), .overflw(CPU_ALU_OVERFLOW_1_overflw));
  CPU_ALU_SIGN_8 CPU_ALU_SIGN_8_1 (.i(CPU_ADDER_8_1_output_bus_1), .negative(CPU_ALU_SIGN_8_1_negative));
  CPU_Z CPU_Z_1 (.i(CPU_ADDER_8_1_output_bus_1), .o(CPU_Z_1_o));
  Multiplexer multiplexer_1 (.in1(CPU_ALU_SIGN_8_1_negative), .out(FLAG_S), .sel(Enable));  // open: in0
  Multiplexer #(.width(8)) multiplexer_2 (.in1(CPU_ADDER_8_1_output_bus_1), .out(C), .sel(Enable));  // open: in0
  Multiplexer multiplexer_3 (.in1(CPU_ADDER_8_1_half_carry_out), .out(FLAG_H), .sel(Enable));  // open: in0
  Multiplexer multiplexer_4 (.in1(1'b0), .out(FLAG_N), .sel(Enable));  // open: in0
  Multiplexer multiplexer_5 (.in1(CPU_Z_1_o), .out(FLAG_Z), .sel(Enable));  // open: in0
  Multiplexer multiplexer_6 (.in1(CPU_ALU_OVERFLOW_1_overflw), .out(FLAG_P_V), .sel(Enable));  // open: in0
  Multiplexer multiplexer_7 (.in1(CPU_ADDER_8_1_carry_out), .out(FLAG_C), .sel(Enable));  // open: in0

  // Notes on the sheet:
  //   A: pull=down
  //   B: pull=down
  //   carry_in: pull=down
  //   FLAG_P_V: pull=down
  //   FLAG_C: pull=down
  //   FLAG_N: pull=down
  //   FLAG_Z: pull=down
  //   C: pull=down
  //   FLAG_H: pull=down
  //   FLAG_S: pull=down
  //   (Parity/Overflow)
  //   (Carry)
  //   (ADD=0, SUB=1)
  //   (Zero)
  //   (Half-Carry)
  //   (Sign)
endmodule

module CPU_SUB (
  input  [7:0] A,
  input  [7:0] B,
  input  Enable,
  output FLAG_P_V,
  output FLAG_C,
  output FLAG_N,
  output FLAG_Z,
  output [7:0] C,
  output FLAG_H,
  output FLAG_S
);

  wire comparator_1_lt, CPU_ADDER_8_1_carry_out, CPU_ALU_OVERFLOW_1_overflw, CPU_ALU_SIGN_8_1_negative,
       CPU_Z_1_o, not_1_out;
  wire [7:0] CPU_ADDER_8_1_output_bus_1, CPU_NOT_1_output_bus_1;

  CPU_NOT CPU_NOT_1 (.i(B), .Output_bus_1(CPU_NOT_1_output_bus_1));
  Comparator #(.width(5)) comparator_1 (.a({1'b0, A[3:0]}), .b({1'b0, B[3:0]}), .lt(comparator_1_lt));  // open: gt, eq
  CPU_ADDER_8 CPU_ADDER_8_1 (
    .a(A), .b(CPU_NOT_1_output_bus_1), .carry_in(1'b1), .carry_out(CPU_ADDER_8_1_carry_out),
    .Output_bus_1(CPU_ADDER_8_1_output_bus_1));  // open: half_carry_out
  CPU_ALU_OVERFLOW CPU_ALU_OVERFLOW_1 (
    .a(A), .b(CPU_NOT_1_output_bus_1), .inp(CPU_ADDER_8_1_output_bus_1), .overflw(CPU_ALU_OVERFLOW_1_overflw));
  CPU_ALU_SIGN_8 CPU_ALU_SIGN_8_1 (.i(CPU_ADDER_8_1_output_bus_1), .negative(CPU_ALU_SIGN_8_1_negative));
  CPU_Z CPU_Z_1 (.i(CPU_ADDER_8_1_output_bus_1), .o(CPU_Z_1_o));
  Multiplexer multiplexer_1 (.in1(CPU_ALU_SIGN_8_1_negative), .out(FLAG_S), .sel(Enable));  // open: in0
  not not_1 (not_1_out, CPU_ADDER_8_1_carry_out);
  Multiplexer #(.width(8)) multiplexer_2 (.in1(CPU_ADDER_8_1_output_bus_1), .out(C), .sel(Enable));  // open: in0
  Multiplexer multiplexer_3 (.in1(comparator_1_lt), .out(FLAG_H), .sel(Enable));  // open: in0
  Multiplexer multiplexer_4 (.in1(1'b1), .out(FLAG_N), .sel(Enable));  // open: in0
  Multiplexer multiplexer_5 (.in1(CPU_Z_1_o), .out(FLAG_Z), .sel(Enable));  // open: in0
  Multiplexer multiplexer_6 (.in1(CPU_ALU_OVERFLOW_1_overflw), .out(FLAG_P_V), .sel(Enable));  // open: in0
  Multiplexer multiplexer_7 (.in1(not_1_out), .out(FLAG_C), .sel(Enable));  // open: in0

  // Notes on the sheet:
  //   FLAG_P_V: pull=down
  //   FLAG_C: pull=down
  //   FLAG_N: pull=down
  //   FLAG_Z: pull=down
  //   C: pull=down
  //   FLAG_H: pull=down
  //   FLAG_S: pull=down
  //   A: pull=down
  //   B: pull=down
  //   (Parity/Overflow)
  //   (Carry)
  //   (Zero)
  //   (Sign)
  //   (ADD=0, SUB=1)
  //   (Half-Carry)
endmodule

module CPU_CP (
  input  [7:0] A,
  input  [7:0] B,
  input  Enable,
  output FLAG_P_V,
  output FLAG_C,
  output FLAG_N,
  output FLAG_Z,
  output FLAG_H,
  output FLAG_S,
  output [7:0] C
);

  wire comparator_1_lt, cpu_adder_8_1_carry_out, cpu_alu_overflow_1_overflw, CPU_ALU_SIGN_8_1_negative,
       CPU_Z_1_o, not_1_out;
  wire [7:0] cpu_adder_8_1_output_bus_1, cpu_not_1_output_bus_1;

  CPU_NOT cpu_not_1 (.i(B), .Output_bus_1(cpu_not_1_output_bus_1));
  Comparator #(.width(5)) comparator_1 (.a({1'b0, A[3:0]}), .b({1'b0, B[3:0]}), .lt(comparator_1_lt));  // open: gt, eq
  CPU_ADDER_8 cpu_adder_8_1 (
    .a(A), .b(cpu_not_1_output_bus_1), .carry_in(1'b1), .carry_out(cpu_adder_8_1_carry_out),
    .Output_bus_1(cpu_adder_8_1_output_bus_1));  // open: half_carry_out
  CPU_ALU_OVERFLOW cpu_alu_overflow_1 (
    .a(A), .b(cpu_not_1_output_bus_1), .inp(cpu_adder_8_1_output_bus_1), .overflw(cpu_alu_overflow_1_overflw));
  CPU_ALU_SIGN_8 CPU_ALU_SIGN_8_1 (.i(cpu_adder_8_1_output_bus_1), .negative(CPU_ALU_SIGN_8_1_negative));
  not not_1 (not_1_out, cpu_adder_8_1_carry_out);
  CPU_Z CPU_Z_1 (.i(cpu_adder_8_1_output_bus_1), .o(CPU_Z_1_o));
  Multiplexer multiplexer_1 (.in1(comparator_1_lt), .out(FLAG_H), .sel(Enable));  // open: in0
  Multiplexer multiplexer_2 (.in1(CPU_ALU_SIGN_8_1_negative), .out(FLAG_S), .sel(Enable));  // open: in0
  Multiplexer multiplexer_3 (.in1(CPU_Z_1_o), .out(FLAG_Z), .sel(Enable));  // open: in0
  Multiplexer #(.width(8)) multiplexer_4 (.in1(A), .out(C), .sel(Enable));  // open: in0
  Multiplexer multiplexer_5 (.in1(not_1_out), .out(FLAG_C), .sel(Enable));  // open: in0
  Multiplexer multiplexer_6 (.in1(1'b1), .out(FLAG_N), .sel(Enable));  // open: in0
  Multiplexer multiplexer_7 (.in1(cpu_alu_overflow_1_overflw), .out(FLAG_P_V), .sel(Enable));  // open: in0

  // Notes on the sheet:
  //   C: pull=down
  //   FLAG_P_V: pull=down
  //   FLAG_C: pull=down
  //   FLAG_N: pull=down
  //   FLAG_Z: pull=down
  //   FLAG_H: pull=down
  //   FLAG_S: pull=down
  //   A: pull=down
  //   B: pull=down
  //   (Parity/Overflow)
  //   (Carry)
  //   (Zero)
  //   (Half-Carry)
  //   (Sign)
  //   (ADD=0, SUB=1)
endmodule

module CPU_AND (
  input  [7:0] a,
  input  [7:0] b,
  input  Enable,
  output [7:0] C,
  output FLAG_Z,
  output FLAG_H,
  output FLAG_C,
  output FLAG_N,
  output FLAG_P_V,
  output FLAG_S
);

  wire cpu_flag_parity_1_out_2, cpu_z_1_o;
  wire [7:0] and_1_out;

  and and_1 (and_1_out[0], a[0], b[0]);
  and and_2 (and_1_out[1], a[1], b[1]);
  and and_3 (and_1_out[2], a[2], b[2]);
  and and_4 (and_1_out[3], a[3], b[3]);
  and and_5 (and_1_out[4], a[4], b[4]);
  and and_6 (and_1_out[5], a[5], b[5]);
  and and_7 (and_1_out[6], a[6], b[6]);
  and and_8 (and_1_out[7], a[7], b[7]);
  CPU_Z cpu_z_1 (.i(and_1_out), .o(cpu_z_1_o));
  CPU_FLAG_PARITY cpu_flag_parity_1 (.i(and_1_out), .out_2(cpu_flag_parity_1_out_2));
  Multiplexer #(.width(8)) multiplexer_1 (.in1(and_1_out), .out(C), .sel(Enable));  // open: in0
  Multiplexer multiplexer_2 (.in1(cpu_z_1_o), .out(FLAG_Z), .sel(Enable));  // open: in0
  Multiplexer multiplexer_3 (.in1(1'b1), .out(FLAG_H), .sel(Enable));  // open: in0
  Multiplexer multiplexer_4 (.in1(1'b0), .out(FLAG_C), .sel(Enable));  // open: in0
  Multiplexer multiplexer_5 (.in1(cpu_flag_parity_1_out_2), .out(FLAG_P_V), .sel(Enable));  // open: in0
  Multiplexer multiplexer_6 (.in1(and_1_out[7]), .out(FLAG_S), .sel(Enable));  // open: in0

  assign FLAG_N = FLAG_C;

  // Notes on the sheet:
  //   C: pull=down
  //   FLAG_Z: pull=down
  //   FLAG_H: pull=down
  //   FLAG_C: pull=down
  //   FLAG_N: pull=down
  //   FLAG_P_V: pull=down
  //   FLAG_S: pull=down
  //   (Zero)
  //   (Carry)
  //   (Sign)
  //   (Half-Carry)
  //   (ADD=0, SUB=1)
endmodule

module CPU_OR (
  input  [7:0] a,
  input  [7:0] b,
  input  Enable,
  output [7:0] C,
  output FLAG_Z,
  output FLAG_H,
  output FLAG_P_V,
  output FLAG_S,
  output FLAG_N,
  output FLAG_C
);

  wire cpu_flag_parity_1_out_2, cpu_z_1_o;
  wire [7:0] or_1_out;

  or or_1 (or_1_out[0], a[0], b[0]);
  or or_2 (or_1_out[1], a[1], b[1]);
  or or_3 (or_1_out[2], a[2], b[2]);
  or or_4 (or_1_out[3], a[3], b[3]);
  or or_5 (or_1_out[4], a[4], b[4]);
  or or_6 (or_1_out[5], a[5], b[5]);
  or or_7 (or_1_out[6], a[6], b[6]);
  or or_8 (or_1_out[7], a[7], b[7]);
  Multiplexer multiplexer_1 (.in1(cpu_z_1_o), .out(FLAG_Z), .sel(Enable));  // open: in0
  CPU_Z cpu_z_1 (.i(or_1_out), .o(cpu_z_1_o));
  CPU_FLAG_PARITY cpu_flag_parity_1 (.i(or_1_out), .out_2(cpu_flag_parity_1_out_2));
  Multiplexer #(.width(8)) multiplexer_2 (.in1(or_1_out), .out(C), .sel(Enable));  // open: in0
  Multiplexer multiplexer_3 (.in1(1'b0), .out(FLAG_H), .sel(Enable));  // open: in0
  Multiplexer multiplexer_4 (.in1(cpu_flag_parity_1_out_2), .out(FLAG_P_V), .sel(Enable));  // open: in0
  Multiplexer multiplexer_5 (.in1(or_1_out[7]), .out(FLAG_S), .sel(Enable));  // open: in0
  Multiplexer multiplexer_6 (.in1(1'b0), .out(FLAG_C), .sel(Enable));  // open: in0

  assign FLAG_N = FLAG_C;

  // Notes on the sheet:
  //   C: pull=down
  //   FLAG_Z: pull=down
  //   FLAG_H: pull=down
  //   FLAG_P_V: pull=down
  //   FLAG_S: pull=down
  //   FLAG_N: pull=down
  //   FLAG_C: pull=down
  //   (Zero)
  //   (Half-Carry)
  //   (Sign)
  //   (Carry)
  //   (ADD=0, SUB=1)
endmodule

module CPU_XOR (
  input  [7:0] a,
  input  [7:0] b,
  input  Enable,
  output FLAG_S,
  output [7:0] c,
  output FLAG_Z,
  output FLAG_P_V,
  output FLAG_C,
  output FLAG_N,
  output FLAG_H
);

  wire cpu_flag_parity_1_out_2, cpu_z_1_o;
  wire [7:0] cpu_xor_1_8_o;

  CPU_XOR_1 cpu_xor_1_1 (.a(a[7]), .b(b[7]), .o(cpu_xor_1_8_o[7]));
  CPU_XOR_1 cpu_xor_1_2 (.a(a[6]), .b(b[6]), .o(cpu_xor_1_8_o[6]));
  CPU_XOR_1 cpu_xor_1_3 (.a(a[5]), .b(b[5]), .o(cpu_xor_1_8_o[5]));
  CPU_XOR_1 cpu_xor_1_4 (.a(a[4]), .b(b[4]), .o(cpu_xor_1_8_o[4]));
  CPU_XOR_1 cpu_xor_1_5 (.a(a[3]), .b(b[3]), .o(cpu_xor_1_8_o[3]));
  CPU_XOR_1 cpu_xor_1_6 (.a(a[2]), .b(b[2]), .o(cpu_xor_1_8_o[2]));
  CPU_XOR_1 cpu_xor_1_7 (.a(a[1]), .b(b[1]), .o(cpu_xor_1_8_o[1]));
  CPU_XOR_1 cpu_xor_1_8 (.a(a[0]), .b(b[0]), .o(cpu_xor_1_8_o[0]));
  Multiplexer multiplexer_1 (.in1(1'b0), .out(FLAG_C), .sel(Enable));  // open: in0
  Multiplexer #(.width(8)) multiplexer_2 (.in1(cpu_xor_1_8_o), .out(c), .sel(Enable));  // open: in0
  CPU_Z cpu_z_1 (.i(cpu_xor_1_8_o), .o(cpu_z_1_o));
  Multiplexer multiplexer_3 (.in1(cpu_z_1_o), .out(FLAG_Z), .sel(Enable));  // open: in0
  Multiplexer multiplexer_4 (.in1(cpu_xor_1_8_o[7]), .out(FLAG_S), .sel(Enable));  // open: in0
  CPU_FLAG_PARITY cpu_flag_parity_1 (.i(cpu_xor_1_8_o), .out_2(cpu_flag_parity_1_out_2));
  Multiplexer multiplexer_5 (.in1(cpu_flag_parity_1_out_2), .out(FLAG_P_V), .sel(Enable));  // open: in0

  assign FLAG_H = FLAG_C;
  assign FLAG_N = FLAG_C;

  // Notes on the sheet:
  //   FLAG_S: pull=down
  //   FLAG_Z: pull=down
  //   FLAG_P_V: pull=down
  //   FLAG_C: pull=down
  //   FLAG_N: pull=down
  //   FLAG_H: pull=down
  //   (Sign)
  //   (Zero)
  //   (Carry)
  //   (ADD=0, SUB=1)
  //   (Half-Carry)
endmodule

module CPU_XOR_1 (
  input  a,
  input  b,
  output o
);

  wire nand_1_out, nand_2_out, not_1_out, not_2_out;

  not not_1 (not_1_out, a);
  not not_2 (not_2_out, b);
  nand nand_1 (nand_1_out, not_1_out, b);
  nand nand_2 (nand_2_out, a, not_2_out);
  nand nand_3 (o, nand_1_out, nand_2_out);
endmodule

module CPU_FLAG_PARITY (
  input  [7:0] i,
  output out_2
);

  wire xor_1_out, xor_2_out, xor_3_out, xor_4_out, xor_5_out, xor_6_out, xor_7_out;

  xor xor_1 (xor_1_out, i[0], i[1]);
  xor xor_2 (xor_2_out, i[2], i[3]);
  xor xor_3 (xor_3_out, i[4], i[5]);
  xor xor_4 (xor_4_out, i[6], i[7]);
  xor xor_5 (xor_5_out, xor_1_out, xor_2_out);
  xor xor_6 (xor_6_out, xor_3_out, xor_4_out);
  xor xor_7 (xor_7_out, xor_5_out, xor_6_out);
  not not_1 (out_2, xor_7_out);
endmodule

module CPU_MEM_1 (
  input  Input_1,
  input  Input_2,
  output Output_1
);

  wire nand_1_out, nand_2_out, nand_4_out;

  nand nand_1 (nand_1_out, Input_1, Input_2);
  nand nand_2 (nand_2_out, nand_1_out, Input_2);
  nand nand_3 (Output_1, nand_1_out, nand_4_out);
  nand nand_4 (nand_4_out, Output_1, nand_2_out);

  // Notes on the sheet:
  //   Input_2: pull=down
  //   Input_1: pull=down
endmodule

module CPU_MEM_8 (
  input  [7:0] Input_bus_1,
  input  Input_1,
  output [7:0] Output_bus_1
);

  CPU_MEM_1 CPU_MEM_1_1 (.Input_2(Input_1), .Input_1(Input_bus_1[0]), .Output_1(Output_bus_1[0]));
  CPU_MEM_1 CPU_MEM_1_8 (.Input_2(Input_1), .Input_1(Input_bus_1[1]), .Output_1(Output_bus_1[1]));
  CPU_MEM_1 CPU_MEM_1_4 (.Input_2(Input_1), .Input_1(Input_bus_1[2]), .Output_1(Output_bus_1[2]));
  CPU_MEM_1 CPU_MEM_1_2 (.Input_2(Input_1), .Input_1(Input_bus_1[3]), .Output_1(Output_bus_1[3]));
  CPU_MEM_1 CPU_MEM_1_7 (.Input_2(Input_1), .Input_1(Input_bus_1[4]), .Output_1(Output_bus_1[4]));
  CPU_MEM_1 CPU_MEM_1_3 (.Input_2(Input_1), .Input_1(Input_bus_1[5]), .Output_1(Output_bus_1[5]));
  CPU_MEM_1 CPU_MEM_1_5 (.Input_2(Input_1), .Input_1(Input_bus_1[6]), .Output_1(Output_bus_1[6]));
  CPU_MEM_1 CPU_MEM_1_6 (.Input_2(Input_1), .Input_1(Input_bus_1[7]), .Output_1(Output_bus_1[7]));

  // Notes on the sheet:
  //   Input_bus_1: pull=down
  //   Input_1: pull=down
  //   Output_bus_1: pull=down
  //   s
endmodule

module CPU_ENABLE_8 (
  input  [7:0] Input_bus_1,
  input  Input_1,
  output [7:0] Output_bus_1
);

  wire and_1_out, and_2_out, and_3_out, and_4_out, and_5_out, and_6_out, and_7_out, and_8_out;

  and and_1 (and_1_out, Input_bus_1[0], Input_1);
  and and_2 (and_2_out, Input_bus_1[1], Input_1);
  and and_3 (and_3_out, Input_bus_1[2], Input_1);
  and and_4 (and_4_out, Input_bus_1[3], Input_1);
  and and_5 (and_5_out, Input_bus_1[4], Input_1);
  and and_6 (and_6_out, Input_bus_1[5], Input_1);
  and and_7 (and_7_out, Input_bus_1[6], Input_1);
  and and_8 (and_8_out, Input_bus_1[7], Input_1);
  Multiplexer multiplexer_1 (.in1(and_1_out), .out(Output_bus_1[0]), .sel(Input_1));  // open: in0
  Multiplexer multiplexer_2 (.in1(and_2_out), .out(Output_bus_1[1]), .sel(Input_1));  // open: in0
  Multiplexer multiplexer_3 (.in1(and_3_out), .out(Output_bus_1[2]), .sel(Input_1));  // open: in0
  Multiplexer multiplexer_4 (.in1(and_4_out), .out(Output_bus_1[3]), .sel(Input_1));  // open: in0
  Multiplexer multiplexer_5 (.in1(and_5_out), .out(Output_bus_1[4]), .sel(Input_1));  // open: in0
  Multiplexer multiplexer_6 (.in1(and_6_out), .out(Output_bus_1[5]), .sel(Input_1));  // open: in0
  Multiplexer multiplexer_7 (.in1(and_7_out), .out(Output_bus_1[6]), .sel(Input_1));  // open: in0
  Multiplexer multiplexer_8 (.in1(and_8_out), .out(Output_bus_1[7]), .sel(Input_1));  // open: in0
endmodule

module CPU_REGISTER_8 (
  input  [7:0] i,
  input  Input_1,
  input  Input_2,
  output [7:0] REG,
  output [7:0] L_0_c20a2d81
);

  wire [7:0] CPU_ENABLE_8_1_output_bus_1;

  CPU_MEM_8 CPU_MEM_8_1 (.Input_bus_1(i), .Input_1(Input_1), .Output_bus_1(REG));
  CPU_ENABLE_8 CPU_ENABLE_8_1 (.Input_bus_1(REG), .Input_1(Input_2), .Output_bus_1(CPU_ENABLE_8_1_output_bus_1));
  Multiplexer #(.width(8)) multiplexer_1 (
    .in1(CPU_ENABLE_8_1_output_bus_1), .out(L_0_c20a2d81), .sel(Input_2));  // open: in0

  // Notes on the sheet:
  //   i: pull=down
  //   Input_1: pull=down
  //   Input_2: pull=down
  //   L_0_c20a2d81: pull=down
  //   s
  //   e
endmodule

module CPU_DECODER_4x16 (
  input  [3:0] in_1,
  output L,
  output out_3,
  output out_4,
  output out_5,
  output out_6,
  output out_7,
  output out_8,
  output out_9,
  output out_10,
  output out_11,
  output out_12,
  output out_13,
  output out_14,
  output out_15,
  output out_16,
  output M
);

  wire not_1_out, not_2_out, not_3_out, not_4_out;

  not not_1 (not_1_out, in_1[0]);
  not not_2 (not_2_out, in_1[1]);
  not not_3 (not_3_out, in_1[2]);
  not not_4 (not_4_out, in_1[3]);
  and and_1 (L, not_4_out, not_3_out, not_2_out, not_1_out);
  and and_2 (out_3, not_4_out, not_3_out, not_2_out, in_1[0]);
  and and_3 (out_4, not_4_out, not_3_out, in_1[1], not_1_out);
  and and_4 (out_5, not_4_out, not_3_out, in_1[1], in_1[0]);
  and and_5 (out_6, not_4_out, in_1[2], not_2_out, not_1_out);
  and and_6 (out_7, not_4_out, in_1[2], not_2_out, in_1[0]);
  and and_7 (out_8, not_4_out, in_1[2], in_1[1], not_1_out);
  and and_8 (out_9, not_4_out, in_1[2], in_1[1], in_1[0]);
  and and_9 (out_10, in_1[3], not_3_out, not_2_out, not_1_out);
  and and_10 (out_11, in_1[3], not_3_out, not_2_out, in_1[0]);
  and and_11 (out_12, in_1[3], not_3_out, in_1[1], not_1_out);
  and and_12 (out_13, in_1[3], not_3_out, in_1[1], in_1[0]);
  and and_13 (out_14, in_1[3], in_1[2], not_2_out, not_1_out);
  and and_14 (out_15, in_1[3], in_1[2], not_2_out, in_1[0]);
  and and_15 (out_16, in_1[3], in_1[2], in_1[1], not_1_out);
  and and_16 (M, in_1[3], in_1[2], in_1[1], in_1[0]);

  // Notes on the sheet:
  //   out_13: pull=down
  //   out_14: pull=down
  //   out_15: pull=down
  //   out_16: pull=down
  //   M: pull=down
  //   L: pull=down
  //   out_3: pull=down
  //   out_4: pull=down
  //   out_5: pull=down
  //   out_6: pull=down
  //   out_7: pull=down
  //   out_8: pull=down
  //   out_9: pull=down
  //   out_10: pull=down
  //   out_11: pull=down
  //   out_12: pull=down
  //   in_1: pull=down
endmodule

module CPU_REG_BYTE (
  input  [7:0] i,
  input  RESET,
  input  h,
  input  v,
  input  s,
  input  e,
  output [7:0] o,
  output [7:0] op
);

  wire and_1_out, and_2_out, and_3_out, or_1_out;
  wire [7:0] cpu_register_8_1_l_0_c20a2d81;

  and and_1 (and_1_out, h, v);
  and and_2 (and_2_out, and_1_out, s);
  and and_3 (and_3_out, and_1_out, e);
  or or_1 (or_1_out, RESET, and_2_out);
  CPU_REGISTER_8 cpu_register_8_1 (
    .i(i), .Input_1(or_1_out), .Input_2(and_3_out), .REG(op), .L_0_c20a2d81(cpu_register_8_1_l_0_c20a2d81));
  Multiplexer #(.width(8)) multiplexer_1 (.in1(cpu_register_8_1_l_0_c20a2d81), .out(o), .sel(and_3_out));  // open: in0

  // Notes on the sheet:
  //   h: pull=down
  //   v: pull=down
  //   s: pull=down
  //   e: pull=down
  //   op: pull=down
  //   RESET: pull=down
  //   i: pull=down
  //   o: pull=down
endmodule

module CPU_NOT (
  input  [7:0] i,
  output [7:0] Output_bus_1
);

  not not_1 (Output_bus_1[0], i[0]);
  not not_2 (Output_bus_1[1], i[1]);
  not not_3 (Output_bus_1[2], i[2]);
  not not_4 (Output_bus_1[3], i[3]);
  not not_5 (Output_bus_1[4], i[4]);
  not not_6 (Output_bus_1[5], i[5]);
  not not_7 (Output_bus_1[6], i[6]);
  not not_8 (Output_bus_1[7], i[7]);
endmodule

module CPU_SHR (
  input  [7:0] i,
  input  shift_in_24438ad9,
  output shift_out_f0cc0400,
  output [7:0] o
);

  wire [7:1] CPU_REGISTER_8_1_l_0_c20a2d81;

  CPU_REGISTER_8 CPU_REGISTER_8_1 (
    .i(i), .Input_1(1'b1), .Input_2(1'b1), .L_0_c20a2d81({CPU_REGISTER_8_1_l_0_c20a2d81, shift_out_f0cc0400}));  // open: REG
  CPU_REGISTER_8 CPU_REGISTER_8_2 (
    .i({shift_in_24438ad9, CPU_REGISTER_8_1_l_0_c20a2d81}), .Input_1(1'b1), .Input_2(1'b1), .L_0_c20a2d81(o));  // open: REG
endmodule

module CPU_SHL (
  input  shift_in_24438ad9,
  input  [7:0] i,
  output [7:0] o,
  output shift_out_f0cc0400
);

  wire [6:0] CPU_REGISTER_8_2_l_0_c20a2d81;

  CPU_REGISTER_8 CPU_REGISTER_8_2 (
    .i(i), .Input_1(1'b1), .Input_2(1'b1), .L_0_c20a2d81({shift_out_f0cc0400, CPU_REGISTER_8_2_l_0_c20a2d81}));  // open: REG
  CPU_REGISTER_8 CPU_REGISTER_8_1 (
    .i({CPU_REGISTER_8_2_l_0_c20a2d81, shift_in_24438ad9}), .Input_1(1'b1), .Input_2(1'b1), .L_0_c20a2d81(o));  // open: REG
endmodule

module CPU_ADDER (
  input  a,
  input  b,
  input  carry_in_155f764b,
  output sum,
  output carry_out_7d7128d5
);

  wire and_1_out, and_2_out, CPU_XOR_1_2_o;

  CPU_XOR_1 CPU_XOR_1_2 (.a(a), .b(b), .o(CPU_XOR_1_2_o));
  and and_1 (and_1_out, carry_in_155f764b, CPU_XOR_1_2_o);
  and and_2 (and_2_out, a, b);
  CPU_XOR_1 CPU_XOR_1_1 (.a(CPU_XOR_1_2_o), .b(carry_in_155f764b), .o(sum));
  or or_1 (carry_out_7d7128d5, and_1_out, and_2_out);
endmodule

module CPU_ADDER_8 (
  input  [7:0] a,
  input  [7:0] b,
  input  carry_in,
  output carry_out,
  output [7:0] Output_bus_1,
  output half_carry_out
);

  wire CPU_ADDER_1_carry_out_7d7128d5, cpu_adder_1_carry_out_7d7128d5_2, CPU_ADDER_3_carry_out_7d7128d5,
       CPU_ADDER_4_carry_out_7d7128d5, CPU_ADDER_5_carry_out_7d7128d5, CPU_ADDER_7_carry_out_7d7128d5;

  CPU_ADDER CPU_ADDER_6 (
    .a(a[7]), .b(b[7]), .carry_in_155f764b(CPU_ADDER_5_carry_out_7d7128d5), .carry_out_7d7128d5(carry_out),
    .sum(Output_bus_1[7]));
  CPU_ADDER CPU_ADDER_5 (
    .a(a[6]), .b(b[6]), .carry_in_155f764b(CPU_ADDER_7_carry_out_7d7128d5),
    .carry_out_7d7128d5(CPU_ADDER_5_carry_out_7d7128d5), .sum(Output_bus_1[6]));
  CPU_ADDER CPU_ADDER_7 (
    .a(a[5]), .b(b[5]), .carry_in_155f764b(CPU_ADDER_4_carry_out_7d7128d5),
    .carry_out_7d7128d5(CPU_ADDER_7_carry_out_7d7128d5), .sum(Output_bus_1[5]));
  CPU_ADDER CPU_ADDER_4 (
    .a(a[4]), .b(b[4]), .carry_in_155f764b(half_carry_out),
    .carry_out_7d7128d5(CPU_ADDER_4_carry_out_7d7128d5), .sum(Output_bus_1[4]));
  CPU_ADDER CPU_ADDER_2 (
    .a(a[3]), .b(b[3]), .carry_in_155f764b(CPU_ADDER_1_carry_out_7d7128d5),
    .carry_out_7d7128d5(half_carry_out), .sum(Output_bus_1[3]));
  CPU_ADDER CPU_ADDER_1 (
    .a(a[2]), .b(b[2]), .carry_in_155f764b(cpu_adder_1_carry_out_7d7128d5_2),
    .carry_out_7d7128d5(CPU_ADDER_1_carry_out_7d7128d5), .sum(Output_bus_1[2]));
  CPU_ADDER cpu_adder_1_dup2 (
    .a(a[1]), .b(b[1]), .carry_in_155f764b(CPU_ADDER_3_carry_out_7d7128d5),
    .carry_out_7d7128d5(cpu_adder_1_carry_out_7d7128d5_2), .sum(Output_bus_1[1]));
  CPU_ADDER CPU_ADDER_3 (
    .a(a[0]), .b(b[0]), .carry_in_155f764b(carry_in), .carry_out_7d7128d5(CPU_ADDER_3_carry_out_7d7128d5),
    .sum(Output_bus_1[0]));
endmodule

module CPU_Z (
  input  [7:0] i,
  output o
);

  wire or_1_out;

  or or_1 (or_1_out, i[0], i[1], i[2], i[3], i[4], i[5], i[6], i[7]);
  not not_1 (o, or_1_out);
endmodule

module CPU_DECODER_3x8 (
  input  [2:0] i,
  output [7:0] o
);

  wire not_1_out, not_2_out, not_3_out;

  not not_1 (not_1_out, i[2]);
  not not_2 (not_2_out, i[1]);
  not not_3 (not_3_out, i[0]);
  and and_1 (o[0], not_3_out, not_2_out, not_1_out);
  and and_2 (o[1], not_3_out, not_2_out, i[2]);
  and and_3 (o[2], not_3_out, i[1], not_1_out);
  and and_4 (o[3], not_3_out, i[1], i[2]);
  and and_5 (o[4], i[0], not_2_out, not_1_out);
  and and_6 (o[5], i[0], not_2_out, i[2]);
  and and_7 (o[6], i[0], i[1], not_1_out);
  and and_8 (o[7], i[0], i[1], i[2]);

  // Notes on the sheet:
  //   o: pull=down
  //   i: pull=down
endmodule
